# Fritzing sketch nano connections (saved by Fritzing 0.8.7b)
breadboards: 1

parts:
  Part1 = Arduino Nano (Rev3.0) (ICSP)
  Part2 = 9 Degrees of Freedom - Sensor Stick

nets:
  GND: Part1.GND, Part2.GND
  N1: Part1.A5, Part2.SCL
  N2: Part1.A4, Part2.SDA
  3V3: Part1.3V3, Part2.VCC
